# Fritzing sketch GeoWatch (saved by Fritzing 0.7.10b)
stripboards: 1

parts:
  J4_Level_shifter_3_3V = female pin header, 9 pins [form="♀ (female)"]
  J9_Level_shifter_5V = female pin header, 9 pins [form="♀ (female)"]
  J10_COMPASS_module = female pin header, 5 pins [form="♀ (female)"]
  J11_GPS_module = female pin header, 4 pins [form="♀ (female)"]
  J12_BLUETOOTH_module = female pin header, 6 pins [form="♀ (female)"]
  J13_OLED_module = female pin header, 7 pins [form="♀ (female)"]
  U1 = Arduino Mega
  J14_Input_select = male pin header, 3 pins [form="♂ (male)"]
  J15_3V_Input = Screw terminal - 2 pins [package=THT]

nets (from the pcb view):
  N1: J4_Level_shifter_3_3V.pin1, J11_GPS_module.pin2, J12_BLUETOOTH_module.pin3
  N2: J4_Level_shifter_3_3V.pin2, J11_GPS_module.pin3
  N3: J4_Level_shifter_3_3V.pin3, J12_BLUETOOTH_module.pin4
  N4: J4_Level_shifter_3_3V.pin4, J12_BLUETOOTH_module.pin5
  N5: J4_Level_shifter_3_3V.pin5, J10_COMPASS_module.pin4
  N6: J4_Level_shifter_3_3V.pin6, J10_COMPASS_module.pin3
  N7: J4_Level_shifter_3_3V.pin7, J13_OLED_module.pin3
  N8: J4_Level_shifter_3_3V.pin8, J13_OLED_module.pin4
  N9: J4_Level_shifter_3_3V.pin9, J10_COMPASS_module.pin1, J11_GPS_module.pin1, J12_BLUETOOTH_module.pin1, J13_OLED_module.pin2, J14_Input_select.pin2
  N10: J9_Level_shifter_5V.pin1, U1.D16
  N11: J9_Level_shifter_5V.pin2, U1.D17
  N12: J9_Level_shifter_5V.pin3, U1.D18
  N13: J9_Level_shifter_5V.pin4, U1.D19
  N14: J9_Level_shifter_5V.pin5, U1.D20
  N15: J9_Level_shifter_5V.pin6, U1.D21
  N16: J9_Level_shifter_5V.pin7, U1.D52
  N17: J9_Level_shifter_5V.pin8, U1.D51
  N18: J9_Level_shifter_5V.pin9, U1.+5V
  N19: J10_COMPASS_module.pin2, J11_GPS_module.pin4, J12_BLUETOOTH_module.pin2, J12_BLUETOOTH_module.pin6, J13_OLED_module.pin1, U1.GND, J15_3V_Input.pin1
  N20: J10_COMPASS_module.pin5, J13_OLED_module.pin5, U1.D5
  N21: J13_OLED_module.pin6, U1.D4
  N22: J13_OLED_module.pin7, U1.D3
  N23: U1.3V3, J14_Input_select.pin3
  N24: J14_Input_select.pin1, J15_3V_Input.pin2
